// Logisim project projetArchi.circ as structural Verilog: 10 circuits, main circuit main
module main (
  output [31:0] out_1
);

  wire clock_1_out, ual_1_zero, unitecontrole_1_alusrc, unitecontrole_1_memwrite, unitecontrole_1_pcsrc,
       unitecontrole_1_regwrite;
  wire [1:0] unitecontrole_1_immsrc, unitecontrole_1_resultsrc;
  wire [31:0] adder_1_out, adder_2_out, extend_1_immresult, instructionmemory_1_instruction,
       multiplexer_1_out, multiplexer_2_out, multiplexer_3_out, register_1_q, registerfile_1_rd1,
       registerfile_1_rd2, ual_1_result;

  Clock clock_1 (.out(clock_1_out));
  Multiplexer #(.width(32)) multiplexer_1 (
    .in0(adder_1_out), .in1(adder_2_out), .out(multiplexer_1_out), .sel(unitecontrole_1_pcsrc));
  Register #(.width(32)) register_1 (.D(multiplexer_1_out), .clk(clock_1_out), .Q(register_1_q));  // open: en, clr
  Adder #(.width(32)) adder_1 (.a(register_1_q), .b(32'h4), .out(adder_1_out));  // open: cin, cout
  InstructionMemory instructionmemory_1 (.Pc(register_1_q), .Instruction(instructionmemory_1_instruction));
  Extend extend_1 (
    .IMMSrc(unitecontrole_1_immsrc), .Imm(instructionmemory_1_instruction[24:0]),
    .ImmResult(extend_1_immresult));
  Adder #(.width(32)) adder_2 (.a(register_1_q), .b(extend_1_immresult), .out(adder_2_out));  // open: cin, cout
  UniteControle unitecontrole_1 (
    .ZERO(ual_1_zero), .op(instructionmemory_1_instruction[6:0]),
    .func3(instructionmemory_1_instruction[14:12]), .func7_5(instructionmemory_1_instruction[26]),
    .PCSrc(unitecontrole_1_pcsrc), .ResultSrc(unitecontrole_1_resultsrc),
    .MemWrite(unitecontrole_1_memwrite), .AluSrc(unitecontrole_1_alusrc), .ImmSrc(unitecontrole_1_immsrc),
    .RegWrite(unitecontrole_1_regwrite));  // open: out_11
  RegisterFile registerfile_1 (
    .WE(unitecontrole_1_regwrite), .clk(clock_1_out), .A1(instructionmemory_1_instruction[24:20]),
    .A2(instructionmemory_1_instruction[19:15]), .A3(instructionmemory_1_instruction[11:7]),
    .Rw(multiplexer_3_out), .RD1(registerfile_1_rd1), .RD2(registerfile_1_rd2));
  Multiplexer #(.width(32)) multiplexer_2 (
    .in0(registerfile_1_rd2), .in1(extend_1_immresult), .out(multiplexer_2_out), .sel(unitecontrole_1_alusrc));
  UAL ual_1 (.A(registerfile_1_rd1), .B(multiplexer_2_out), .ZERO(ual_1_zero), .Result(ual_1_result));
  DataMemory datamemory_1 (
    .WE(unitecontrole_1_memwrite), .clk(clock_1_out), .A1(ual_1_result), .Donnee(registerfile_1_rd2),
    .Donnees(out_1));
  Multiplexer #(.select(2), .width(32)) multiplexer_3 (
    .in0(ual_1_result), .in1(out_1), .in2(adder_1_out), .out(multiplexer_3_out),
    .sel(unitecontrole_1_resultsrc));  // open: in3
endmodule

module UniteControle (
  input  ZERO,
  input  [6:0] op,
  input  [2:0] func3,
  input  func7_5,
  output PCSrc,
  output [1:0] ResultSrc,
  output MemWrite,
  output AluSrc,
  output [1:0] ImmSrc,
  output RegWrite,
  output [2:0] out_11
);

  wire and_1_out, and_2_out, and_6_out, and_7_out, and_8_out, and_9_out, and_10_out, and_11_out, and_12_out,
       and_13_out, and_14_out, and_15_out, and_16_out, and_18_out, and_19_out, and_20_out, not_1_out,
       not_2_out, not_3_out, not_4_out, not_5_out, not_6_out, not_7_out, not_8_out, not_9_out, not_10_out,
       not_11_out, not_12_out, not_13_out, not_14_out, not_15_out, not_16_out, not_17_out, not_18_out,
       not_19_out, not_20_out, not_21_out, not_22_out, not_23_out, not_24_out, not_25_out, not_26_out,
       not_27_out, not_28_out, not_29_out, not_30_out, not_31_out, not_32_out, not_33_out, not_34_out,
       not_35_out, not_36_out, not_37_out, not_38_out, not_39_out, not_40_out, not_41_out, not_42_out,
       not_43_out, not_44_out, not_45_out, not_46_out, not_47_out, not_48_out, not_49_out, not_50_out,
       not_51_out, not_52_out, not_53_out, not_54_out, not_55_out;
  wire [2:0] or_2_out;

  not not_1 (not_1_out, op[2]);
  not not_2 (not_2_out, op[3]);
  not not_3 (not_3_out, op[4]);
  not not_4 (not_4_out, op[2]);
  not not_5 (not_5_out, op[0]);
  not not_6 (not_6_out, op[1]);
  not not_7 (not_7_out, op[2]);
  not not_8 (not_8_out, op[3]);
  not not_9 (not_9_out, op[4]);
  not not_10 (not_10_out, op[2]);
  not not_11 (not_11_out, op[0]);
  not not_12 (not_12_out, op[2]);
  not not_13 (not_13_out, op[3]);
  not not_14 (not_14_out, op[4]);
  not not_15 (not_15_out, op[0]);
  not not_16 (not_16_out, op[1]);
  not not_17 (not_17_out, op[2]);
  not not_18 (not_18_out, op[3]);
  not not_19 (not_19_out, op[4]);
  not not_20 (not_20_out, op[0]);
  not not_21 (not_21_out, op[1]);
  not not_22 (not_22_out, op[3]);
  not not_23 (not_23_out, op[4]);
  not not_24 (not_24_out, op[0]);
  not not_25 (not_25_out, op[2]);
  not not_26 (not_26_out, op[3]);
  not not_27 (not_27_out, op[4]);
  not not_28 (not_28_out, op[0]);
  not not_29 (not_29_out, op[2]);
  not not_30 (not_30_out, op[3]);
  not not_31 (not_31_out, op[4]);
  not not_32 (not_32_out, op[2]);
  not not_33 (not_33_out, op[2]);
  not not_34 (not_34_out, op[3]);
  not not_35 (not_35_out, op[4]);
  not not_36 (not_36_out, op[6]);
  not not_37 (not_37_out, op[2]);
  not not_38 (not_38_out, op[0]);
  not not_39 (not_39_out, op[1]);
  not not_40 (not_40_out, op[2]);
  not not_41 (not_41_out, op[3]);
  not not_42 (not_42_out, op[4]);
  not not_43 (not_43_out, op[0]);
  not not_44 (not_44_out, op[3]);
  not not_45 (not_45_out, op[4]);
  not not_46 (not_46_out, op[0]);
  not not_47 (not_47_out, op[1]);
  not not_48 (not_48_out, op[3]);
  not not_49 (not_49_out, op[4]);
  not not_50 (not_50_out, func3[0]);
  not not_51 (not_51_out, func3[1]);
  not not_52 (not_52_out, func3[2]);
  not not_53 (not_53_out, func3[0]);
  not not_54 (not_54_out, func3[2]);
  not not_55 (not_55_out, func3[0]);
  and and_1 (and_1_out, op[0], op[1], not_1_out, not_2_out, not_3_out, op[5], op[6]);
  and and_2 (and_2_out, op[0], op[1], not_4_out, op[3], op[4], op[5], op[6]);
  and and_3 (ResultSrc[0], not_5_out, not_6_out, not_7_out, not_8_out, not_9_out, op[5], op[6]);
  and and_4 (ResultSrc[1], op[0], op[1], not_10_out, op[3], op[4], op[5], op[6]);
  and and_5 (MemWrite, not_11_out, op[1], not_12_out, not_13_out, not_14_out, op[5], op[6]);
  and and_6 (and_6_out, not_15_out, not_16_out, not_17_out, not_18_out, not_19_out, op[5], op[6]);
  and and_7 (and_7_out, not_20_out, not_21_out, op[2], not_22_out, not_23_out, op[5], op[6]);
  and and_8 (and_8_out, not_24_out, op[1], not_25_out, not_26_out, not_27_out, op[5], op[6]);
  and and_9 (and_9_out, not_28_out, op[1], not_29_out, not_30_out, not_31_out, op[5], op[6]);
  and and_10 (and_10_out, op[0], op[1], not_32_out, op[3], op[4], op[5], op[6]);
  and and_11 (and_11_out, op[0], op[1], not_33_out, not_34_out, not_35_out, op[5], not_36_out);
  and and_12 (and_12_out, op[0], op[1], not_37_out, op[3], op[4], op[5], op[6]);
  and and_13 (and_13_out, not_38_out, not_39_out, not_40_out, not_41_out, not_42_out, op[5], op[6]);
  and and_14 (and_14_out, not_43_out, op[1], op[2], not_44_out, not_45_out, op[5], op[6]);
  and and_15 (and_15_out, not_46_out, not_47_out, op[2], not_48_out, not_49_out, op[5], op[6]);
  and and_16 (and_16_out, op[5], func7_5, not_50_out, not_51_out, not_52_out);
  and and_17 (or_2_out[2], not_53_out, func3[1], not_54_out);
  and and_18 (and_18_out, func3[2], func3[1], not_55_out);
  and and_19 (and_19_out, func3[2], func3[1], func3[0]);
  and and_20 (and_20_out, ZERO, and_1_out);
  or or_1 (ImmSrc[0], and_9_out, and_10_out);
  or or_2 (or_2_out[0], and_16_out, or_2_out[2], and_18_out);
  or or_3 (or_2_out[1], and_18_out, and_19_out);
  or or_4 (PCSrc, and_20_out, and_2_out);
  or or_5 (AluSrc, and_6_out, and_7_out, and_8_out);
  or or_6 (ImmSrc[1], and_11_out, and_12_out);
  or or_7 (RegWrite, and_13_out, and_14_out, and_15_out);
  Multiplexer #(.select(2), .width(3)) multiplexer_1 (
    .in0(3'b000), .in1(3'b001), .in2(or_2_out), .out(out_11), .sel(op[1:0]));  // open: in3
endmodule

module UAL (
  input  [31:0] A,
  input  [31:0] B,
  output ZERO,
  output [31:0] Result
);

  wire [31:0] adder_1_out, and_1_out, bit_extender_1_out, or_1_out, subtractor_1_out;

  Adder #(.width(32)) adder_1 (.a(A), .b(B), .out(adder_1_out));  // open: cin, cout
  nor nor_1 (ZERO, subtractor_1_out[0], subtractor_1_out[1], subtractor_1_out[2], subtractor_1_out[3], subtractor_1_out[4], subtractor_1_out[5], subtractor_1_out[6], subtractor_1_out[7], subtractor_1_out[8], subtractor_1_out[9], subtractor_1_out[10], subtractor_1_out[11], subtractor_1_out[12], subtractor_1_out[13], subtractor_1_out[14], subtractor_1_out[15], subtractor_1_out[17], subtractor_1_out[18], subtractor_1_out[19], subtractor_1_out[20], subtractor_1_out[21], subtractor_1_out[22], subtractor_1_out[23], subtractor_1_out[24], subtractor_1_out[25], subtractor_1_out[26], subtractor_1_out[27], subtractor_1_out[28], subtractor_1_out[29], subtractor_1_out[30], subtractor_1_out[31], subtractor_1_out[16]);
  Subtractor #(.width(32)) subtractor_1 (.a(A), .b(B), .out(subtractor_1_out));  // open: bin, bout
  assign and_1_out = A & B;  // AND_Gate and_1, 32 bits wide
  Multiplexer #(.select(3), .width(32)) multiplexer_1 (
    .in0(adder_1_out), .in1(subtractor_1_out), .in2(and_1_out), .in3(or_1_out), .in4(bit_extender_1_out),
    .in5({32{1'b0}}), .in6({32{1'b0}}), .in7({32{1'b0}}), .out(Result));  // open: sel
  assign or_1_out = A | B;  // OR_Gate or_1, 32 bits wide
  assign bit_extender_1_out = {{30{1'b0}}, {1'b0, subtractor_1_out[31]}};  // Bit_Extender bit_extender_1
endmodule

module InstructionMemory16Mx32 (
  input  [27:0] PC,
  output [31:0] out_2
);

  wire [31:0] rom_1_data, rom_2_data, rom_3_data, rom_4_data, rom_5_data, rom_6_data, rom_7_data, rom_8_data,
       rom_9_data, rom_10_data, rom_11_data, rom_12_data, rom_13_data, rom_14_data, rom_15_data, rom_16_data;

  ROM #(.addrWidth(24), .dataWidth(32)) rom_1 (.addr(PC[23:0]), .data(rom_1_data));
  ROM #(.addrWidth(24), .dataWidth(32)) rom_2 (.addr(PC[23:0]), .data(rom_2_data));
  ROM #(.addrWidth(24), .dataWidth(32)) rom_3 (.addr(PC[23:0]), .data(rom_3_data));
  ROM #(.addrWidth(24), .dataWidth(32)) rom_4 (.addr(PC[23:0]), .data(rom_4_data));
  ROM #(.addrWidth(24), .dataWidth(32)) rom_5 (.addr(PC[23:0]), .data(rom_5_data));
  ROM #(.addrWidth(24), .dataWidth(32)) rom_6 (.addr(PC[23:0]), .data(rom_6_data));
  ROM #(.addrWidth(24), .dataWidth(32)) rom_7 (.addr(PC[23:0]), .data(rom_7_data));
  ROM #(.addrWidth(24), .dataWidth(32)) rom_8 (.addr(PC[23:0]), .data(rom_8_data));
  ROM #(.addrWidth(24), .dataWidth(32)) rom_9 (.addr(PC[23:0]), .data(rom_9_data));
  ROM #(.addrWidth(24), .dataWidth(32)) rom_10 (.addr(PC[23:0]), .data(rom_10_data));
  ROM #(.addrWidth(24), .dataWidth(32)) rom_11 (.addr(PC[23:0]), .data(rom_11_data));
  ROM #(.addrWidth(24), .dataWidth(32)) rom_12 (.addr(PC[23:0]), .data(rom_12_data));
  ROM #(.addrWidth(24), .dataWidth(32)) rom_13 (.addr(PC[23:0]), .data(rom_13_data));
  ROM #(.addrWidth(24), .dataWidth(32)) rom_14 (.addr(PC[23:0]), .data(rom_14_data));
  ROM #(.addrWidth(24), .dataWidth(32)) rom_15 (.addr(PC[23:0]), .data(rom_15_data));
  ROM #(.addrWidth(24), .dataWidth(32)) rom_16 (.addr(PC[23:0]), .data(rom_16_data));
  Multiplexer #(.select(4), .width(32)) multiplexer_1 (
    .in0(rom_1_data), .in1(rom_2_data), .in2(rom_3_data), .in3(rom_4_data), .in4(rom_5_data),
    .in5(rom_6_data), .in6(rom_7_data), .in7(rom_8_data), .in8(rom_9_data), .in9(rom_10_data),
    .in10(rom_11_data), .in11(rom_12_data), .in12(rom_13_data), .in13(rom_14_data), .in14(rom_15_data),
    .in15(rom_16_data), .out(out_2), .sel(PC[27:24]));

  // Notes on the sheet:
  //   contents of rom_1 (hex, n*v repeats v):
  //   64a423
endmodule

module InstructionMemory (
  input  [31:0] Pc,
  output [31:0] Instruction
);

  wire [31:0] instructionmemory16mx32_1_out_2, instructionmemory16mx32_2_out_2,
       instructionmemory16mx32_3_out_2, instructionmemory16mx32_4_out_2, instructionmemory16mx32_5_out_2,
       instructionmemory16mx32_6_out_2, instructionmemory16mx32_7_out_2, instructionmemory16mx32_8_out_2,
       instructionmemory16mx32_9_out_2, instructionmemory16mx32_10_out_2, instructionmemory16mx32_11_out_2,
       instructionmemory16mx32_12_out_2, instructionmemory16mx32_13_out_2, instructionmemory16mx32_14_out_2,
       instructionmemory16mx32_15_out_2, instructionmemory16mx32_16_out_2;

  InstructionMemory16Mx32 instructionmemory16mx32_1 (.PC(Pc[27:0]), .out_2(instructionmemory16mx32_1_out_2));
  InstructionMemory16Mx32 instructionmemory16mx32_2 (.PC(Pc[27:0]), .out_2(instructionmemory16mx32_2_out_2));
  InstructionMemory16Mx32 instructionmemory16mx32_3 (.PC(Pc[27:0]), .out_2(instructionmemory16mx32_3_out_2));
  InstructionMemory16Mx32 instructionmemory16mx32_4 (.PC(Pc[27:0]), .out_2(instructionmemory16mx32_4_out_2));
  InstructionMemory16Mx32 instructionmemory16mx32_5 (.PC(Pc[27:0]), .out_2(instructionmemory16mx32_5_out_2));
  InstructionMemory16Mx32 instructionmemory16mx32_6 (.PC(Pc[27:0]), .out_2(instructionmemory16mx32_6_out_2));
  InstructionMemory16Mx32 instructionmemory16mx32_7 (.PC(Pc[27:0]), .out_2(instructionmemory16mx32_7_out_2));
  InstructionMemory16Mx32 instructionmemory16mx32_8 (.PC(Pc[27:0]), .out_2(instructionmemory16mx32_8_out_2));
  InstructionMemory16Mx32 instructionmemory16mx32_9 (.PC(Pc[27:0]), .out_2(instructionmemory16mx32_9_out_2));
  InstructionMemory16Mx32 instructionmemory16mx32_10 (.PC(Pc[27:0]), .out_2(instructionmemory16mx32_10_out_2));
  InstructionMemory16Mx32 instructionmemory16mx32_11 (.PC(Pc[27:0]), .out_2(instructionmemory16mx32_11_out_2));
  InstructionMemory16Mx32 instructionmemory16mx32_12 (.PC(Pc[27:0]), .out_2(instructionmemory16mx32_12_out_2));
  InstructionMemory16Mx32 instructionmemory16mx32_13 (.PC(Pc[27:0]), .out_2(instructionmemory16mx32_13_out_2));
  InstructionMemory16Mx32 instructionmemory16mx32_14 (.PC(Pc[27:0]), .out_2(instructionmemory16mx32_14_out_2));
  InstructionMemory16Mx32 instructionmemory16mx32_15 (.PC(Pc[27:0]), .out_2(instructionmemory16mx32_15_out_2));
  InstructionMemory16Mx32 instructionmemory16mx32_16 (.PC(Pc[27:0]), .out_2(instructionmemory16mx32_16_out_2));
  Multiplexer #(.select(4), .width(32)) multiplexer_1 (
    .in0(instructionmemory16mx32_1_out_2), .in1(instructionmemory16mx32_2_out_2),
    .in2(instructionmemory16mx32_3_out_2), .in3(instructionmemory16mx32_4_out_2),
    .in4(instructionmemory16mx32_5_out_2), .in5(instructionmemory16mx32_6_out_2),
    .in6(instructionmemory16mx32_7_out_2), .in7(instructionmemory16mx32_8_out_2),
    .in8(instructionmemory16mx32_9_out_2), .in9(instructionmemory16mx32_10_out_2),
    .in10(instructionmemory16mx32_11_out_2), .in11(instructionmemory16mx32_12_out_2),
    .in12(instructionmemory16mx32_13_out_2), .in13(instructionmemory16mx32_14_out_2),
    .in14(instructionmemory16mx32_15_out_2), .in15(instructionmemory16mx32_16_out_2), .out(Instruction),
    .sel(Pc[31:28]));
endmodule

module RegisterFile8VS32 (
  input  clk,
  input  We,
  input  [2:0] A1,
  input  [2:0] A2,
  input  [31:0] Donnee,
  input  in_6,
  input  in_7,
  input  in_8,
  input  in_9,
  input  in_10,
  input  in_11,
  input  in_12,
  input  in_13,
  output [31:0] RD1,
  output [31:0] RD2
);

  wire and_1_out, and_2_out, and_3_out, and_4_out, and_5_out, and_6_out, and_7_out, and_8_out;
  wire [31:0] register_1_q, register_2_q, register_3_q, register_4_q, register_5_q, register_6_q,
       register_7_q, register_8_q;

  and and_1 (and_1_out, in_6, clk);
  and and_2 (and_2_out, in_7, clk);
  and and_3 (and_3_out, in_8, clk);
  and and_4 (and_4_out, in_9, clk);
  and and_5 (and_5_out, in_10, clk);
  and and_6 (and_6_out, in_11, clk);
  and and_7 (and_7_out, in_12, clk);
  and and_8 (and_8_out, in_13, clk);
  Register #(.width(32)) register_1 (.D(Donnee), .en(We), .clk(and_1_out), .Q(register_1_q));  // open: clr
  Register #(.width(32)) register_2 (.D(Donnee), .en(We), .clk(and_2_out), .Q(register_2_q));  // open: clr
  Register #(.width(32)) register_3 (.D(Donnee), .en(We), .clk(and_3_out), .Q(register_3_q));  // open: clr
  Register #(.width(32)) register_4 (.D(Donnee), .en(We), .clk(and_4_out), .Q(register_4_q));  // open: clr
  Register #(.width(32)) register_5 (.D(Donnee), .en(We), .clk(and_5_out), .Q(register_5_q));  // open: clr
  Register #(.width(32)) register_6 (.D(Donnee), .en(We), .clk(and_6_out), .Q(register_6_q));  // open: clr
  Register #(.width(32)) register_7 (.D(Donnee), .en(We), .clk(and_7_out), .Q(register_7_q));  // open: clr
  Register #(.width(32)) register_8 (.D(Donnee), .en(We), .clk(and_8_out), .Q(register_8_q));  // open: clr
  Multiplexer #(.select(3), .width(32)) multiplexer_1 (
    .in0(register_1_q), .in1(register_2_q), .in2(register_3_q), .in3(register_4_q), .in4(register_5_q),
    .in5(register_6_q), .in6(register_7_q), .in7(register_8_q), .out(RD1), .sel(A1));
  Multiplexer #(.select(3), .width(32)) multiplexer_2 (
    .in0(register_1_q), .in1(register_2_q), .in2(register_3_q), .in3(register_4_q), .in4(register_5_q),
    .in5(register_6_q), .in6(register_7_q), .in7(register_8_q), .out(RD2), .sel(A2));
endmodule

module RegisterFile (
  input  WE,
  input  clk,
  input  [4:0] A1,
  input  [4:0] A2,
  input  [4:0] A3,
  input  [31:0] Rw,
  output [31:0] RD1,
  output [31:0] RD2
);

  wire and_1_out, and_2_out, and_3_out, and_4_out, and_5_out, and_6_out, and_7_out, and_8_out,
       decoder_1_out0, decoder_1_out1, decoder_1_out2, decoder_1_out3, decoder_1_out4, decoder_1_out5,
       decoder_1_out6, decoder_1_out7, decoder_2_out0, decoder_2_out1, decoder_2_out2, decoder_2_out3,
       decoder_2_out4, decoder_2_out5, decoder_2_out6, decoder_2_out7, decoder_3_out0, decoder_3_out1,
       decoder_3_out2, decoder_3_out3, decoder_3_out4, decoder_3_out5, decoder_3_out6, decoder_3_out7,
       decoder_4_out0, decoder_4_out1, decoder_4_out2, decoder_4_out3, decoder_4_out4, decoder_4_out5,
       decoder_4_out6, decoder_4_out7, not_1_out, not_2_out, not_3_out, not_4_out;
  wire [31:0] registerfile8vs32_1_rd1, registerfile8vs32_1_rd2, registerfile8vs32_2_rd1,
       registerfile8vs32_2_rd2, registerfile8vs32_3_rd1, registerfile8vs32_3_rd2, registerfile8vs32_4_rd1,
       registerfile8vs32_4_rd2;

  Decoder #(.select(3)) decoder_1 (
    .out0(decoder_1_out0), .out1(decoder_1_out1), .out2(decoder_1_out2), .out3(decoder_1_out3),
    .out4(decoder_1_out4), .out5(decoder_1_out5), .out6(decoder_1_out6), .out7(decoder_1_out7), .sel(A3[2:0]));  // open: en
  Decoder #(.select(3)) decoder_2 (
    .out0(decoder_2_out0), .out1(decoder_2_out1), .out2(decoder_2_out2), .out3(decoder_2_out3),
    .out4(decoder_2_out4), .out5(decoder_2_out5), .out6(decoder_2_out6), .out7(decoder_2_out7), .sel(A3[2:0]));  // open: en
  Decoder #(.select(3)) decoder_3 (
    .out0(decoder_3_out0), .out1(decoder_3_out1), .out2(decoder_3_out2), .out3(decoder_3_out3),
    .out4(decoder_3_out4), .out5(decoder_3_out5), .out6(decoder_3_out6), .out7(decoder_3_out7), .sel(A3[2:0]));  // open: en
  Decoder #(.select(3)) decoder_4 (
    .out0(decoder_4_out0), .out1(decoder_4_out1), .out2(decoder_4_out2), .out3(decoder_4_out3),
    .out4(decoder_4_out4), .out5(decoder_4_out5), .out6(decoder_4_out6), .out7(decoder_4_out7), .sel(A3[2:0]));  // open: en
  not not_1 (not_1_out, A3[4]);
  not not_2 (not_2_out, A3[4]);
  not not_3 (not_3_out, A3[3]);
  not not_4 (not_4_out, A3[3]);
  and and_1 (and_1_out, not_1_out, not_3_out);
  and and_2 (and_2_out, not_2_out, A3[3]);
  and and_3 (and_3_out, A3[4], not_4_out);
  and and_4 (and_4_out, A3[4], A3[3]);
  and and_5 (and_5_out, and_1_out, WE);
  and and_6 (and_6_out, and_2_out, WE);
  and and_7 (and_7_out, and_3_out, WE);
  and and_8 (and_8_out, and_4_out, WE);
  RegisterFile8VS32 registerfile8vs32_1 (
    .clk(clk), .We(and_5_out), .A1(A1[2:0]), .A2(A2[2:0]), .Donnee(Rw), .in_6(decoder_1_out0),
    .in_7(decoder_1_out1), .in_8(decoder_1_out2), .in_9(decoder_1_out3), .in_10(decoder_1_out4),
    .in_11(decoder_1_out5), .in_12(decoder_1_out6), .in_13(decoder_1_out7), .RD1(registerfile8vs32_1_rd1),
    .RD2(registerfile8vs32_1_rd2));
  RegisterFile8VS32 registerfile8vs32_2 (
    .clk(clk), .We(and_6_out), .A1(A1[2:0]), .A2(A2[2:0]), .Donnee(Rw), .in_6(decoder_2_out0),
    .in_7(decoder_2_out1), .in_8(decoder_2_out2), .in_9(decoder_2_out3), .in_10(decoder_2_out4),
    .in_11(decoder_2_out5), .in_12(decoder_2_out6), .in_13(decoder_2_out7), .RD1(registerfile8vs32_2_rd1),
    .RD2(registerfile8vs32_2_rd2));
  RegisterFile8VS32 registerfile8vs32_3 (
    .clk(clk), .We(and_7_out), .A1(A1[2:0]), .A2(A2[2:0]), .Donnee(Rw), .in_6(decoder_3_out0),
    .in_7(decoder_3_out1), .in_8(decoder_3_out2), .in_9(decoder_3_out3), .in_10(decoder_3_out4),
    .in_11(decoder_3_out5), .in_12(decoder_3_out6), .in_13(decoder_3_out7), .RD1(registerfile8vs32_3_rd1),
    .RD2(registerfile8vs32_3_rd2));
  RegisterFile8VS32 registerfile8vs32_4 (
    .clk(clk), .We(and_8_out), .A1(A1[2:0]), .A2(A2[2:0]), .Donnee(Rw), .in_6(decoder_4_out0),
    .in_7(decoder_4_out1), .in_8(decoder_4_out2), .in_9(decoder_4_out3), .in_10(decoder_4_out4),
    .in_11(decoder_4_out5), .in_12(decoder_4_out6), .in_13(decoder_4_out7), .RD1(registerfile8vs32_4_rd1),
    .RD2(registerfile8vs32_4_rd2));
  Multiplexer #(.select(2), .width(32)) multiplexer_1 (
    .in0(registerfile8vs32_1_rd2), .in1(registerfile8vs32_2_rd1), .in2(registerfile8vs32_3_rd1),
    .in3(registerfile8vs32_4_rd1), .out(RD1), .sel(A1[4:3]));
  Multiplexer #(.select(2), .width(32)) multiplexer_2 (
    .in0(registerfile8vs32_1_rd1), .in1(registerfile8vs32_2_rd2), .in2(registerfile8vs32_3_rd2),
    .in3(registerfile8vs32_4_rd2), .out(RD2), .sel(A2[4:3]));
endmodule

module DataMemoryVS32 (
  input  clk,
  input  WE,
  input  [27:0] A1,
  input  [31:0] Donnee,
  output [31:0] out_5
);

  wire and_1_out, and_2_out, and_3_out, and_4_out, and_5_out, and_6_out, and_7_out, and_8_out, and_9_out,
       and_10_out, and_11_out, and_12_out, and_13_out, and_14_out, and_15_out, and_16_out, decoder_1_out0,
       decoder_1_out1, decoder_1_out2, decoder_1_out3, decoder_1_out4, decoder_1_out5, decoder_1_out6,
       decoder_1_out7, decoder_1_out8, decoder_1_out9, decoder_1_out10, decoder_1_out11, decoder_1_out12,
       decoder_1_out13, decoder_1_out14, decoder_1_out15;
  wire [31:0] ram_1_dout, ram_2_dout, ram_3_dout, ram_4_dout, ram_5_dout, ram_6_dout, ram_7_dout, ram_8_dout,
       ram_9_dout, ram_10_dout, ram_11_dout, ram_12_dout, ram_13_dout, ram_14_dout, ram_15_dout, ram_16_dout;

  Decoder #(.select(4)) decoder_1 (
    .out0(decoder_1_out0), .out1(decoder_1_out1), .out2(decoder_1_out2), .out3(decoder_1_out3),
    .out4(decoder_1_out4), .out5(decoder_1_out5), .out6(decoder_1_out6), .out7(decoder_1_out7),
    .out8(decoder_1_out8), .out9(decoder_1_out9), .out10(decoder_1_out10), .out11(decoder_1_out11),
    .out12(decoder_1_out12), .out13(decoder_1_out13), .out14(decoder_1_out14), .out15(decoder_1_out15),
    .sel(A1[27:24]));  // open: en
  RAM #(.addrWidth(24), .dataWidth(32)) ram_1 (
    .addr(A1[23:0]), .we(and_1_out), .clk(clk), .din(Donnee), .dout(ram_1_dout));  // open: oe
  and and_1 (and_1_out, decoder_1_out0, WE);
  RAM #(.addrWidth(24), .dataWidth(32)) ram_2 (
    .addr(A1[23:0]), .we(and_2_out), .clk(clk), .din(Donnee), .dout(ram_2_dout));  // open: oe
  and and_2 (and_2_out, decoder_1_out1, WE);
  RAM #(.addrWidth(24), .dataWidth(32)) ram_3 (
    .addr(A1[23:0]), .we(and_3_out), .clk(clk), .din(Donnee), .dout(ram_3_dout));  // open: oe
  and and_3 (and_3_out, decoder_1_out2, WE);
  RAM #(.addrWidth(24), .dataWidth(32)) ram_4 (
    .addr(A1[23:0]), .we(and_4_out), .clk(clk), .din(Donnee), .dout(ram_4_dout));  // open: oe
  and and_4 (and_4_out, decoder_1_out3, WE);
  RAM #(.addrWidth(24), .dataWidth(32)) ram_5 (
    .addr(A1[23:0]), .we(and_5_out), .clk(clk), .din(Donnee), .dout(ram_5_dout));  // open: oe
  and and_5 (and_5_out, decoder_1_out4, WE);
  RAM #(.addrWidth(24), .dataWidth(32)) ram_6 (
    .addr(A1[23:0]), .we(and_6_out), .clk(clk), .din(Donnee), .dout(ram_6_dout));  // open: oe
  and and_6 (and_6_out, decoder_1_out5, WE);
  RAM #(.addrWidth(24), .dataWidth(32)) ram_7 (
    .addr(A1[23:0]), .we(and_7_out), .clk(clk), .din(Donnee), .dout(ram_7_dout));  // open: oe
  and and_7 (and_7_out, decoder_1_out6, WE);
  RAM #(.addrWidth(24), .dataWidth(32)) ram_8 (
    .addr(A1[23:0]), .we(and_8_out), .clk(clk), .din(Donnee), .dout(ram_8_dout));  // open: oe
  and and_8 (and_8_out, decoder_1_out7, WE);
  RAM #(.addrWidth(24), .dataWidth(32)) ram_9 (
    .addr(A1[23:0]), .we(and_9_out), .clk(clk), .din(Donnee), .dout(ram_9_dout));  // open: oe
  and and_9 (and_9_out, decoder_1_out8, WE);
  RAM #(.addrWidth(24), .dataWidth(32)) ram_10 (
    .addr(A1[23:0]), .we(and_10_out), .clk(clk), .din(Donnee), .dout(ram_10_dout));  // open: oe
  and and_10 (and_10_out, decoder_1_out9, WE);
  RAM #(.addrWidth(24), .dataWidth(32)) ram_11 (
    .addr(A1[23:0]), .we(and_11_out), .clk(clk), .din(Donnee), .dout(ram_11_dout));  // open: oe
  and and_11 (and_11_out, decoder_1_out10, WE);
  RAM #(.addrWidth(24), .dataWidth(32)) ram_12 (
    .addr(A1[23:0]), .we(and_12_out), .clk(clk), .din(Donnee), .dout(ram_12_dout));  // open: oe
  and and_12 (and_12_out, decoder_1_out11, WE);
  RAM #(.addrWidth(24), .dataWidth(32)) ram_13 (
    .addr(A1[23:0]), .we(and_13_out), .clk(clk), .din(Donnee), .dout(ram_13_dout));  // open: oe
  and and_13 (and_13_out, decoder_1_out12, WE);
  RAM #(.addrWidth(24), .dataWidth(32)) ram_14 (
    .addr(A1[23:0]), .we(and_14_out), .clk(clk), .din(Donnee), .dout(ram_14_dout));  // open: oe
  and and_14 (and_14_out, decoder_1_out13, WE);
  RAM #(.addrWidth(24), .dataWidth(32)) ram_15 (
    .addr(A1[23:0]), .we(and_15_out), .clk(clk), .din(Donnee), .dout(ram_15_dout));  // open: oe
  and and_15 (and_15_out, decoder_1_out14, WE);
  RAM #(.addrWidth(24), .dataWidth(32)) ram_16 (
    .addr(A1[23:0]), .we(and_16_out), .clk(clk), .din(Donnee), .dout(ram_16_dout));  // open: oe
  and and_16 (and_16_out, decoder_1_out15, WE);
  Multiplexer #(.select(4), .width(32)) multiplexer_1 (
    .in0(ram_1_dout), .in1(ram_2_dout), .in2(ram_3_dout), .in3(ram_4_dout), .in4(ram_5_dout),
    .in5(ram_6_dout), .in6(ram_7_dout), .in7(ram_8_dout), .in8(ram_9_dout), .in9(ram_10_dout),
    .in10(ram_11_dout), .in11(ram_12_dout), .in12(ram_13_dout), .in13(ram_14_dout), .in14(ram_15_dout),
    .in15(ram_16_dout), .out(out_5), .sel(A1[27:24]));
endmodule

module DataMemory (
  input  WE,
  input  clk,
  input  [31:0] A1,
  input  [31:0] Donnee,
  output [31:0] Donnees
);

  wire and_1_out, and_2_out, and_3_out, and_4_out, and_5_out, and_6_out, and_7_out, and_8_out, and_9_out,
       and_10_out, and_11_out, and_12_out, and_13_out, and_14_out, and_15_out, and_16_out, decoder_1_out0,
       decoder_1_out1, decoder_1_out2, decoder_1_out3, decoder_1_out4, decoder_1_out5, decoder_1_out6,
       decoder_1_out7, decoder_1_out8, decoder_1_out9, decoder_1_out10, decoder_1_out11, decoder_1_out12,
       decoder_1_out13, decoder_1_out14, decoder_1_out15;
  wire [31:0] datamemoryvs32_1_out_5, datamemoryvs32_2_out_5, datamemoryvs32_3_out_5, datamemoryvs32_4_out_5,
       datamemoryvs32_5_out_5, datamemoryvs32_6_out_5, datamemoryvs32_7_out_5, datamemoryvs32_8_out_5,
       datamemoryvs32_9_out_5, datamemoryvs32_10_out_5, datamemoryvs32_11_out_5, datamemoryvs32_12_out_5,
       datamemoryvs32_13_out_5, datamemoryvs32_14_out_5, datamemoryvs32_15_out_5, datamemoryvs32_16_out_5;

  Decoder #(.select(4)) decoder_1 (
    .out0(decoder_1_out0), .out1(decoder_1_out1), .out2(decoder_1_out2), .out3(decoder_1_out3),
    .out4(decoder_1_out4), .out5(decoder_1_out5), .out6(decoder_1_out6), .out7(decoder_1_out7),
    .out8(decoder_1_out8), .out9(decoder_1_out9), .out10(decoder_1_out10), .out11(decoder_1_out11),
    .out12(decoder_1_out12), .out13(decoder_1_out13), .out14(decoder_1_out14), .out15(decoder_1_out15),
    .sel(A1[31:28]));  // open: en
  and and_1 (and_1_out, WE, decoder_1_out0);
  and and_2 (and_2_out, WE, decoder_1_out1);
  and and_3 (and_3_out, decoder_1_out2, WE);
  and and_4 (and_4_out, WE, decoder_1_out3);
  and and_5 (and_5_out, WE, decoder_1_out4);
  and and_6 (and_6_out, WE, decoder_1_out5);
  and and_7 (and_7_out, WE, decoder_1_out6);
  and and_8 (and_8_out, WE, decoder_1_out7);
  and and_9 (and_9_out, WE, decoder_1_out8);
  and and_10 (and_10_out, WE, decoder_1_out9);
  and and_11 (and_11_out, WE, decoder_1_out10);
  and and_12 (and_12_out, WE, decoder_1_out11);
  and and_13 (and_13_out, WE, decoder_1_out12);
  and and_14 (and_14_out, WE, decoder_1_out13);
  and and_15 (and_15_out, WE, decoder_1_out14);
  and and_16 (and_16_out, WE, decoder_1_out15);
  DataMemoryVS32 datamemoryvs32_1 (
    .clk(clk), .WE(and_1_out), .A1(A1[27:0]), .Donnee(Donnee), .out_5(datamemoryvs32_1_out_5));
  DataMemoryVS32 datamemoryvs32_2 (
    .clk(clk), .WE(and_2_out), .A1(A1[27:0]), .Donnee(Donnee), .out_5(datamemoryvs32_2_out_5));
  DataMemoryVS32 datamemoryvs32_3 (
    .clk(clk), .WE(and_3_out), .A1(A1[27:0]), .Donnee(Donnee), .out_5(datamemoryvs32_3_out_5));
  DataMemoryVS32 datamemoryvs32_4 (
    .clk(clk), .WE(and_4_out), .A1(A1[27:0]), .Donnee(Donnee), .out_5(datamemoryvs32_4_out_5));
  DataMemoryVS32 datamemoryvs32_5 (
    .clk(clk), .WE(and_5_out), .A1(A1[27:0]), .Donnee(Donnee), .out_5(datamemoryvs32_5_out_5));
  DataMemoryVS32 datamemoryvs32_6 (
    .clk(clk), .WE(and_6_out), .A1(A1[27:0]), .Donnee(Donnee), .out_5(datamemoryvs32_6_out_5));
  DataMemoryVS32 datamemoryvs32_7 (
    .clk(clk), .WE(and_7_out), .A1(A1[27:0]), .Donnee(Donnee), .out_5(datamemoryvs32_7_out_5));
  DataMemoryVS32 datamemoryvs32_8 (
    .clk(clk), .WE(and_8_out), .A1(A1[27:0]), .Donnee(Donnee), .out_5(datamemoryvs32_8_out_5));
  DataMemoryVS32 datamemoryvs32_9 (
    .clk(clk), .WE(and_9_out), .A1(A1[27:0]), .Donnee(Donnee), .out_5(datamemoryvs32_9_out_5));
  DataMemoryVS32 datamemoryvs32_10 (
    .clk(clk), .WE(and_10_out), .A1(A1[27:0]), .Donnee(Donnee), .out_5(datamemoryvs32_10_out_5));
  DataMemoryVS32 datamemoryvs32_11 (
    .clk(clk), .WE(and_11_out), .A1(A1[27:0]), .Donnee(Donnee), .out_5(datamemoryvs32_11_out_5));
  DataMemoryVS32 datamemoryvs32_12 (
    .clk(clk), .WE(and_12_out), .A1(A1[27:0]), .Donnee(Donnee), .out_5(datamemoryvs32_12_out_5));
  DataMemoryVS32 datamemoryvs32_13 (
    .clk(clk), .WE(and_13_out), .A1(A1[27:0]), .Donnee(Donnee), .out_5(datamemoryvs32_13_out_5));
  DataMemoryVS32 datamemoryvs32_14 (
    .clk(clk), .WE(and_14_out), .A1(A1[27:0]), .Donnee(Donnee), .out_5(datamemoryvs32_14_out_5));
  DataMemoryVS32 datamemoryvs32_15 (
    .clk(clk), .WE(and_15_out), .A1(A1[27:0]), .Donnee(Donnee), .out_5(datamemoryvs32_15_out_5));
  DataMemoryVS32 datamemoryvs32_16 (
    .clk(clk), .WE(and_16_out), .A1(A1[27:0]), .Donnee(Donnee), .out_5(datamemoryvs32_16_out_5));
  Multiplexer #(.select(4), .width(32)) multiplexer_1 (
    .in0(datamemoryvs32_1_out_5), .in1(datamemoryvs32_2_out_5), .in2(datamemoryvs32_3_out_5),
    .in3(datamemoryvs32_4_out_5), .in4(datamemoryvs32_5_out_5), .in5(datamemoryvs32_6_out_5),
    .in6(datamemoryvs32_7_out_5), .in7(datamemoryvs32_8_out_5), .in8(datamemoryvs32_9_out_5),
    .in9(datamemoryvs32_10_out_5), .in10(datamemoryvs32_11_out_5), .in11(datamemoryvs32_12_out_5),
    .in12(datamemoryvs32_13_out_5), .in13(datamemoryvs32_14_out_5), .in14(datamemoryvs32_15_out_5),
    .in15(datamemoryvs32_16_out_5), .out(Donnees), .sel(A1[31:28]));
endmodule

module Extend (
  input  [1:0] IMMSrc,
  input  [24:0] Imm,
  output [31:0] ImmResult
);

  wire [31:0] bit_extender_1_out, bit_extender_2_out, bit_extender_3_out;

  assign bit_extender_1_out = {{20{Imm[24]}}, Imm[24:13]};  // Bit_Extender bit_extender_1
  assign bit_extender_2_out = {{19{Imm[24]}}, {Imm[24:23], Imm[0], Imm[22:18], Imm[5:2], 1'b0}};  // Bit_Extender bit_extender_2
  assign bit_extender_3_out = {{20{Imm[24]}}, {Imm[24:18], Imm[4:0]}};  // Bit_Extender bit_extender_3
  Multiplexer #(.select(2), .width(32)) multiplexer_1 (
    .in0(bit_extender_1_out), .in1(bit_extender_3_out), .in2(bit_extender_2_out), .in3({32{1'b0}}),
    .out(ImmResult), .sel(IMMSrc));
endmodule
